# Fritzing sketch Cirucito_Nano_Schema (saved by Fritzing 0.9.2b)
breadboards: 1

parts:
  Componente1 = Arduino Nano (Rev3.0)
  Componente2 = SRF05 Ultrasonic Rangefinder
  U1 = LCD-16X2 [package=lcd-16x2]
  Batteria = Battery block 9V
  J1 = Piezo Speaker
  Pot = POT [package=pot_mammoth]
  ON-OFF = Momentary Switch [package=ksa_sealed_tac_switch]
  R1 = Resistor [tolerance=±5% resistance=220 package="0402 [SMD]"]
  C1 = Electrolytic Capacitor [capacitance=100µF package="200 mil [THT, electrolytic]"]
  Laser_Switch = Momentary Switch [package=ksa_sealed_tac_switch]
  Laser_1 = LEDs [package=led10mm]
  Laser_2 = LEDs [package=led10mm]
  R3 = Resistor [tolerance=±5% resistance=220 package="0402 [SMD]"]
  R2 = Resistor [tolerance=±5% resistance=220 package="0402 [SMD]"]
  LEDR = LEDs [package=led10mm]
  LEDG = LEDs [package=led10mm]
  Misurazione = Pushbutton [package=THT]
  Compensazione = Pushbutton [package=THT]
  R4 = Resistor [tolerance=±5% resistance=10k package="0402 [SMD]"]
  R5 = Resistor [tolerance=±5% resistance=10k package="0402 [SMD]"]

nets:
  GND: Componente1.GND, Componente2.GND, U1.VSS, U1.E, U1.K, Batteria.-, J1.pin1, Pot.A, C1.-, Laser_2.C, R3.Pin_1, R2.Pin_1, R4.Pin_0, R5.Pin_0
  N1: Componente1.D2, LEDG.A
  N2: Componente1.D3, U1.VO
  N3: Componente1.D4, LEDR.A
  N4: Componente1.D5, U1.RS
  N5: Componente1.D6, U1.R_W
  N6: Componente1.D7, U1.DB0
  N7: Componente1.D8, U1.DB1
  N8: Componente1.D9, Componente2.Trig
  N9: Componente1.D10, U1.DB2
  N10: Componente1.D11/MOSI, U1.DB3
  N11: Componente1.D12/MISO, U1.DB4
  N12: Componente1.VIN, ON-OFF.3
  5V: Componente1.5V, Componente1.A1, Componente2.VCC, U1.VDD, Pot.E, R1.Pin_1, C1.+, Laser_Switch.1, Misurazione.leg1, Compensazione.leg1
  N13: Componente1.A5, J1.pin2
  N14: Componente1.A4, Misurazione.leg0, R4.Pin_1
  N15: Componente1.A3, Compensazione.leg0, R5.Pin_1
  N16: Componente1.A2, Componente2.Echo
  N17: Componente1.A0, Pot.S
  N18: U1.A, R1.Pin_0
  N19: Batteria.+, ON-OFF.1
  N20: Laser_Switch.3, Laser_1.A
  N21: Laser_1.C, Laser_2.A
  N22: R3.Pin_0, LEDG.C
  N23: R2.Pin_0, LEDR.C
